# Fritzing sketch Storm (saved by Fritzing 0.9.0b)
breadboards: 1

parts:
  T1 = LM35 Temperature Sensor [package="TO92 [THT]"]
  Part1 = Arduino Ethernet Shield (Rev3)
  R1 = Photocell (LDR) [package=THT]
  R2 = Resistor [tolerance=±5% resistance=1k package=THT]
  Part2 = Arduino Uno (Rev3)  # not connected

nets:
  N1: T1.+Vs, Part1.5V, R1.pin_0
  N2: T1.Vout, Part1.A0
  GND: T1.GND, Part1.GND, R2.Pin_0
  N3: Part1.A1, R1.pin_1, R2.Pin_1
